# Fritzing sketch Robot (saved by Fritzing 1.0.2b)
circuit board: 8.46667cm x 5.64444cm
breadboards: 1

parts:
  Pico_2W = Raspberry Pi Pico W
  R1 = Resistor [tolerance=±5% power=0.25W resistance=100 package=THT]
  TSAL6200 = LED - 5mm [color="Infrared (940nm)" current=0.030A package="5 mm [THT]"]
  2N2222 = npn-Powertransistor [package="TO220 [THT]"]
  R2_1000_Ohms = 1000 Ω Resistor [package=THT]
  BPW34 = S1133 Si Photodiode [package="8mm Ceramic [THT]"]
  R2 = Resistor [tolerance=±5% power=0.25W resistance=100000 package=THT]
  MCP6002 = LM 358 Dual Op-Amp [package="DIP8 [THT]"]
  R3 = Resistor [tolerance=±5% power=0.25W resistance=1000000 package=THT]
  MCP6002_2 = LM 358 Dual Op-Amp [package="DIP8 [THT]"]
  MCP6002_3 = LM 358 Dual Op-Amp [package="DIP8 [THT]"]
  BPW34_2 = S1133 Si Photodiode [package="8mm Ceramic [THT]"]
  BPW34_3 = S1133 Si Photodiode [package="8mm Ceramic [THT]"]
  R4 = Resistor [tolerance=±5% power=0.25W resistance=100000 package=THT]
  R5 = Resistor [tolerance=±5% power=0.25W resistance=100000 package=THT]
  R6 = Resistor [tolerance=±5% power=0.25W resistance=1000000 package=THT]
  R7 = Resistor [tolerance=±5% power=0.25W resistance=1000000 package=THT]
  SG90 = Basic Servo
  5V_2A_Power_Supply = Power plug
  BNO085 = Adafruit BNO085 9-DOF Orientation IMU Fusion [part_number="Addfruit #4754"]

nets:
  N1: Pico_2W.pin_1, SG90.pulse
  GND: Pico_2W.pin_3, Pico_2W.pin_8, Pico_2W.pin_13, Pico_2W.pin_18, Pico_2W.pin_23, Pico_2W.pin_28, Pico_2W.pin_33, Pico_2W.pin_38, Pico_2W.pin_42, 2N2222.emitter, BPW34.anode, MCP6002.connector2, MCP6002.connector3, MCP6002_2.connector2, MCP6002_2.connector3, MCP6002_3.connector2, MCP6002_3.connector3, BPW34_2.anode, BPW34_3.anode, SG90.gnd, 5V_2A_Power_Supply.GND, BNO085.GND
  N2: Pico_2W.pin_6, BNO085.SCL/SCK/RX
  N3: Pico_2W.pin_7, BNO085.SDA/MISO/TX
  N4: Pico_2W.pin_29, R2_1000_Ohms.Pin_1
  N5: Pico_2W.pin_31, MCP6002_3.connector0, R7.Pin_0
  N6: Pico_2W.pin_32, MCP6002_2.connector0, R6.Pin_0
  N7: Pico_2W.pin_34, MCP6002.connector0, R3.Pin_0
  N8: Pico_2W.pin_36, R2.Pin_1, MCP6002.connector7, MCP6002_2.connector7, MCP6002_3.connector7, R4.Pin_1, R5.Pin_1, BNO085.VCC
  VCC: Pico_2W.pin_39, TSAL6200.anode, SG90.vcc, 5V_2A_Power_Supply.VCC
  N9: R1.Pin_0, TSAL6200.cathode
  N10: R1.Pin_1, 2N2222.collector
  N11: 2N2222.base, R2_1000_Ohms.Pin_0
  N12: BPW34.cathode, R2.Pin_0, MCP6002.connector1, R3.Pin_1
  N13: MCP6002_2.connector1, BPW34_2.cathode, R4.Pin_0, R6.Pin_1
  N14: MCP6002_3.connector1, BPW34_3.cathode, R5.Pin_0, R7.Pin_1

custom parts:
  Raspberry Pi Pico W: Raspberry Pi Pico W. Based around the RP2040 microcontroller the Pico W is a low cost microcontroller device bringing Raspberry Pi quality, cost, and easy of use to the microcontroller space. The areas marked KEEPOUT in pcb silkscreen should not have traces running through them to avoid shorts on a soldered in module!
  1000 Ω Resistor: A generic resistor (0.25W)
